# Fritzing sketch Smart_Dormitory (saved by Fritzing 0.9.3b)

parts:
  A1 = WeMos D1 R1
  J1 = Basic Servo
  BAT1 = 12 battery [package=battery]

nets:
  N1: A1.Pin_9, J1.vcc
  N2: A1.Pin_11, A1.Pin_13, A1.Pin_32, J1.gnd, BAT1.-
  N3: A1.Pin_15, BAT1.+
  N4: A1.Pin_48, J1.pulse

custom parts:
  WeMos D1 R1: The WeMos D1 is a ESP8266 WiFi based board that uses the Arduino layout with a operating voltage of 3.3V.
  12 battery: 12V lead acid type battery, like the Husqvarna YTH2448 12V 35AH battery. This is the mini version 1/4 the size of the actual battery to be closer to typical breadboard parts (around 2in wide rathher than 7in). The pads in pcb are sized to accomidate up to 14ga wire (as these batterys will deliver high currents.)
